# Fritzing sketch Block Diagram (saved by Fritzing 0.8.7b)
breadboards: 2

parts:
  FRDM-KL25Z2 = FRDM-KL25Z [part_number=FRDM-KL25Z]
  Mod5 = KY-003 Hall Magnetic Sensor Module [package="Breakout board"]
  Parte2 = SRF05 Ultrasonic Rangefinder
  F2 = Fan - Ventilador [package=THT]
  KY-2 = Keyes Relay [package=THT]
  Mod6 = KY-015 Temperature & Humidity Sensor Module [package="Breakout board"]
  U2 = ESP8266 NodeMCU LoLin module
  Q2 = PNP-Transistor [package="TO92 [THT]"]
  VCC3 = Battery block 9V
  LCD2 = LCD screen
  J4 = Basic Servo
  J5 = Basic Servo
  J6 = Basic Servo
  Matrix_keypad2 = KEYPAD 4x4
  R1 = Trimmer Potentiometer [maximum_resistance=10kΩ package=THT]

nets:
  N1: FRDM-KL25Z2.A0_PTB0, Mod6.S
  N2: FRDM-KL25Z2.A1_PTB1, Mod5.S
  N3: FRDM-KL25Z2.A2_PTB2, Parte2.Trig
  N4: FRDM-KL25Z2.A3_PTB3, Parte2.Echo
  N5: FRDM-KL25Z2.A4_PTC2, Matrix_keypad2.col3
  N6: FRDM-KL25Z2.A5_PTC1, Matrix_keypad2.col2
  N7: FRDM-KL25Z2.D2_PTD4, LCD2.DB4
  N8: FRDM-KL25Z2.D3_PTA12_PWM, J6.pulse
  N9: FRDM-KL25Z2.D4_PTA4, J5.pulse
  N10: FRDM-KL25Z2.D5_PTA5_PWM, J4.pulse
  N11: FRDM-KL25Z2.D9_PTD5_PWM, LCD2.DB5
  N12: FRDM-KL25Z2.D10_PTD0_PWM, LCD2.RS
  N13: FRDM-KL25Z2.D11_PTD2_PWM, U2.S1
  N14: FRDM-KL25Z2.D12_PTD3, LCD2.E
  N15: FRDM-KL25Z2.D13_PTD1, LCD2.R/W
  GND: FRDM-KL25Z2.GND, FRDM-KL25Z2.GND2, FRDM-KL25Z2.GND3, Mod5.-, Parte2.GND, Mod6.-, LCD2.VSS, LCD2.LED-, R1.leg2
  VIN: FRDM-KL25Z2.5V_P5V_USB, Mod5.Vin, Parte2.VCC, Mod6.Vin, LCD2.VDD, LCD2.LED+, R1.leg1
  N16: FRDM-KL25Z2.P3V3, FRDM-KL25Z2.P3V3_2, Q2.E
  N17: F2.5V, KY-2.NO
  N18: F2.GND, VCC3.-
  N19: KY-2.signal, Q2.C
  VCC: KY-2.power, J4.vcc, J5.vcc, J6.vcc
  GND_2: KY-2.ground, J4.gnd, J5.gnd, J6.gnd
  N20: LCD2.V0, R1.wiper

custom parts:
  FRDM-KL25Z: Freedom Board, based on basic pinout of Arduino Rev.3. Attention: the board is NOT 5V compatible.
  KY-003 Hall Magnetic Sensor Module: KEYES KY-003 Arduino Hall Magnetic Sensor Module is a switch that will turn on/off in the presence of a magnetic field.
  Fan - Ventilador: Ventilador de 2 pines, se encuentra comunmente en computadoras de escritorio
  Keyes Relay: The Keyes 5V relay module is suitable for SCM development, home appliance control. It uses a 5V~12V TIL control signal which can control DC / AC signal.
  KY-015 Temperature & Humidity Sensor Module: KY-015 temperature and humidity sensor module, provides a low-latency serial interface to measure humidity and temperature.
  ESP8266 NodeMCU LoLin module: ESP8266 based NodeMCU
  KEYPAD 4x4: Matrix keypad 16 buttons, 4 rows x 4 columns
